# Fritzing sketch wiring (saved by Fritzing 0.9.6b)
perfboards: 1

parts:
  DFPlayer_Mini1 = DFPlayer MINI [package="DIP (Dual Inline) [THT]"]
  J2 = JST XH_2.54mm Horizontal SMD Connector 3pin [package=SMD]
  CONN1 = USB connector [package=THT]
  J1 = JST XH_2.54mm Horizontal SMD_Connector 2pin [package=SMD]
  A1 = Waveshare rp2040-zero tht [package=THT]
  J1_2 = JST XH_2.54mm Horizontal SMD Connector 3pin [package=SMD]
  J3 = JST XH_2.54mm Horizontal SMD Connector 3pin [package=SMD]

nets:
  N1: DFPlayer_Mini1.RX, A1.Pin_19
  N2: DFPlayer_Mini1.DAC_R, J3.pin1
  N3: DFPlayer_Mini1.DAC_L, J3.pin3
  N4: J2.pin1, A1.Pin_5
  N5: J2.pin2, CONN1.5V
  N6: CONN1.d+, J1.pin2, A1.Pin_1
  N7: A1.Pin_3, J1_2.pin3
  N8: A1.Pin_22, J1_2.pin1
  N9: J1_2.pin2, J3.pin2

notes:
  USB Power

custom parts:
  DFPlayer MINI: MP3 module by DFRobot.com for playing Music from an SD-Card. Supports WAV and MP3 files.
  JST XH_2.54mm Horizontal SMD Connector 3pin: JST XH_2.54mm Horizontal SMD Connector 3pin.
  JST XH_2.54mm Horizontal SMD_Connector 2pin: JST XH_2.54mm Horizontal SMD_Connector 2pin.
  Waveshare rp2040-zero tht: .RP2040-Zero, A Low-Cost, High-Performance Pico-Like MCU Board Based On Raspberry Pi Microcontroller RP2040. This varant is THT without the extra connections.
